# Fritzing sketch tvout (saved by Fritzing 0.7.12b)
breadboards: 1

parts:
  Nano1 = Arduino Nano v2.3  # not connected
  R1 = Resistor [tolerance=±5% resistance=1k package=THT]
  R2 = Resistor [tolerance=±5% resistance=470 package=THT]

nets:
  N1: R1.Pin_1, R2.Pin_1

notes:
  Video Signal
  Video GND
